# Fritzing sketch ArduariumuyDiagramV3 (saved by Fritzing 0.9.1b)
breadboards: 1

parts:
  Part1 = Arduino Uno (Rev3)
  Q1 = NPN-Transistor [package="TO92 [THT]"]
  R1 = Resistor [tolerance=±5% resistance=220 package=THT]
  Q2 = PNP-Transistor [package="TO92 [THT]"]
  LCD1 = LCD screen  # not connected
  Power_plug1 = Power plug  # not connected
  LED1 = LED - 5mm [color="Red (633nm)" package="5 mm [THT]"]
  Part2 = Serial Alphanumeric Display Driver  # not connected
  Part3 = Real Time Clock Module - DS1307 RTC Breakout Board  # not connected
  S1 = Round Pushbutton  # not connected

nets:
  N1: Part1.D9_PWM, Q1.E
  N2: Part1.GND, Q1.C, Q2.E, Q2.C
  N3: Q1.B, LED1.cathode
  N4: R1.Pin_1, Q2.B

notes:
  SDA
  SCL
  sensor de temp
  TIP120
  12v
